# Fritzing sketch Butterfly_Alarm_Clock (saved by Fritzing 0.9.3b)
circuit board: 8.46667cm x 5.64444cm
stripboards: 1

parts:
  Clock = DeadOn RTC - DS3234 Breakout
  LED1 = RGB LED (com. cathode, rgb) [package="5 mm [THT]"]
  J1 = Power Jack [package=power_jack_smd]
  R4 = PHOTOCELL [package=photocell-kit]
  R5 = Resistor [tolerance=±5% resistance=10k package=THT]
  LED3 = RGB LED (com. cathode, rgb) [package="5 mm [THT]"]
  LED4 = RGB LED (com. cathode, rgb) [package="5 mm [THT]"]
  R2 = Resistor [tolerance=±5% resistance=100 package=THT]
  R1 = Resistor [tolerance=±5% resistance=100 package=THT]
  R3 = Resistor [tolerance=±5% resistance=150 package=THT]
  LED2 = RGB LED (com. cathode, rgb) [package="5 mm [THT]"]
  Arduino = Arduino Pro Mini (3.3V)

nets:
  SS: Clock.SS, Arduino.D10
  MOSI: Clock.MOSI, Arduino.MOSI
  MISO: Clock.MISO, Arduino.MISO
  SCK: Clock.SCLK, Arduino.SCK
  5V: Clock.VCC, J1.PWR, R4.P$1, Arduino.VCC
  GND: Clock.GND, LED1.common_cathode, J1.GND, J1.GNDBREAK, R5.Pin_0, LED3.common_cathode, LED4.common_cathode, LED2.common_cathode, Arduino.GND
  N1: LED1.red_anode, LED3.red_anode, LED4.red_anode, R3.Pin_0, LED2.red_anode
  N2: LED1.green_anode, LED3.green_anode, LED4.green_anode, R2.Pin_0, LED2.green_anode
  N3: LED1.blue_anode, LED3.blue_anode, LED4.blue_anode, R1.Pin_0, LED2.blue_anode
  N4: R4.P$2, R5.Pin_1, Arduino.A1
  Green: R2.Pin_1, Arduino.D6
  Blue: R1.Pin_1, Arduino.D3
  Red: R3.Pin_1, Arduino.D9

notes:
  Butterfly Alarm Clock, Alarm clock for toddler, 1
